// Logisim project ALU8.circ as structural Verilog: 9 circuits, main circuit main
module main (
  input  [7:0] A,
  input  [7:0] B,
  input  Cin,
  input  [3:0] Op,
  output Cout,
  output ZF,
  output SF,
  output OF,
  output [7:0] F
);

  ALU alu_1 (.A(A), .B(B), .Cin(Cin), .Cout(Cout), .OF(ZF), .ZF(SF), .SF(OF), .Op(Op), .F(F));
endmodule

module ALU (
  input  [7:0] A,
  input  [7:0] B,
  input  Cin,
  input  [3:0] Op,
  output ZF,
  output Cout,
  output OF,
  output SF,
  output [7:0] F
);

  wire [7:0] ADD_f, AND_f, SHIFT_LEFT_f, SHIFT_RIGHT_f, SUB_f, undriven, XOR_f;

  addl ADD (.Cin(Cin), .A(A), .B(B), .F(ADD_f));  // open: OF, Cout
  subl SUB (.A(A), .B(B), .Cin(Cin), .F(SUB_f));  // open: Cout, OF
  andl AND (.A(A), .B(B), .F(AND_f));  // open: OF
  xorl XOR (.A(A), .B(undriven), .F(XOR_f));  // open: OF
  asrl SHIFT_RIGHT (.A(A), .F(SHIFT_RIGHT_f));  // open: Cout, OF
  lsll SHIFT_LEFT (.A(A), .F(SHIFT_LEFT_f));  // open: Cout, OF
  Multiplexer #(.select(4), .width(8), .enable("false")) multiplexer_1 (
    .in0(ADD_f), .in1(SUB_f), .in2(AND_f), .in3(XOR_f), .in4(SHIFT_RIGHT_f), .in5(SHIFT_LEFT_f),
    .out({8{F[7]}}), .sel(Op));  // open: in6, in7, in8, in9, in10, in11, in12, in13, in14, in15

  assign F[6:0] = {7{F[7]}};
  assign SF = F[7];
  assign ZF = F[7];
endmodule

module andl (
  input  [7:0] A,
  input  [7:0] B,
  output OF,
  output [7:0] F
);

  assign F = A & B;  // AND_Gate and_1, 8 bits wide

  assign OF = 1'b0;
endmodule

module xorl (
  input  [7:0] A,
  input  [7:0] B,
  output OF,
  output [7:0] F
);

  assign F = A ^ B;  // XOR_Gate xor_1, 8 bits wide

  assign OF = 1'b0;
endmodule

module addl (
  input  Cin,
  input  [7:0] B,
  input  [7:0] A,
  output OF,
  output [7:0] F,
  output Cout
);

  wire adder_1_cout, adder_2_cout, adder_3_cout, adder_4_cout, adder_5_cout, adder_6_cout, adder_7_cout;
  wire [0:0] undriven;

  adder adder_1 (.B(B[1]), .Cin(adder_2_cout), .Out(F[1]), .Cout(adder_1_cout));  // open: A
  adder adder_2 (.A(undriven[0]), .B(B[0]), .Cin(Cin), .Out(F[0]), .Cout(adder_2_cout));
  adder adder_3 (.B(B[3]), .Cin(adder_4_cout), .Out(F[3]), .Cout(adder_3_cout));  // open: A
  adder adder_4 (.B(B[2]), .Cin(adder_1_cout), .Out(F[2]), .Cout(adder_4_cout));  // open: A
  adder adder_5 (.B(B[4]), .Cin(adder_3_cout), .Out(F[4]), .Cout(adder_5_cout));  // open: A
  adder adder_6 (.B(B[5]), .Cin(adder_5_cout), .Out(F[5]), .Cout(adder_6_cout));  // open: A
  adder adder_7 (.B(B[6]), .Cin(adder_6_cout), .Out(F[6]), .Cout(adder_7_cout));  // open: A
  adder adder_8 (.B(B[7]), .Cin(adder_7_cout), .Out(F[7]), .Cout(Cout));  // open: A
endmodule

module subl (
  input  [7:0] A,
  input  [7:0] B,
  input  Cin,
  output Cout,
  output OF,
  output [7:0] F
);
endmodule

module asrl (
  input  [7:0] A,
  output Cout,
  output OF,
  output [7:0] F
);
endmodule

module lsll (
  input  [7:0] A,
  output Cout,
  output OF,
  output [7:0] F
);
endmodule

module adder (
  input  A,
  input  B,
  input  Cin,
  output Out,
  output Cout
);

  wire and_1_out, and_2_out, xor_1_out;

  xor xor_1 (xor_1_out, A, B);
  and and_1 (and_1_out, xor_1_out, Cin);
  and and_2 (and_2_out, A, B);
  xor xor_2 (Out, xor_1_out, Cin);
  or or_1 (Cout, and_1_out, and_2_out);
endmodule
